# Fritzing sketch CS-11M-Step1-LEDs (saved by Fritzing 0.9.3b)
breadboards: 1

parts:
  R4 = Resistor [tolerance=±5% resistance=560 package=THT]
  LED3 = LED - 5mm [color="Red (633nm)" package="5 mm [THT]"]
  LED2 = LED - 5mm [color="Red (633nm)" package="5 mm [THT]"]
  R1 = Resistor [tolerance=±5% resistance=560 package=THT]
  Part1 = Arduino Uno (Rev3)
  R2 = Resistor [tolerance=±5% resistance=560 package=THT]
  R3 = Resistor [tolerance=±5% resistance=560 package=THT]
  LED1 = LED - 5mm [color="Red (633nm)" package="5 mm [THT]"]
  LED4 = LED - 5mm [color="Red (633nm)" package="5 mm [THT]"]

nets:
  N1: R4.Pin_0, LED4.cathode
  N2: R4.Pin_1, R1.Pin_1, Part1.GND, R2.Pin_1
  N3: LED3.cathode, R3.Pin_0
  N4: LED3.anode, Part1.D7
  N5: LED2.cathode, R2.Pin_0
  N6: LED2.anode, Part1.D4
  N7: R1.Pin_0, LED1.cathode
  N8: Part1.D8, LED4.anode
  N9: Part1.D2, LED1.anode
