# Fritzing sketch CS-11M-Step2-Buttons (saved by Fritzing 0.9.3b)
breadboards: 1

parts:
  Part1 = Arduino Uno (Rev3)
  S1 = Pushbutton [package="[THT]"]
  S2 = Pushbutton [package="[THT]"]

nets:
  N1: Part1.D12/MISO, S1.Pin_3, S1.Pin_4
  N2: Part1.D13/SCK, S2.Pin_3, S2.Pin_4
  N3: Part1.GND, S1.Pin_1, S1.Pin_2, S2.Pin_1, S2.Pin_2
