# Fritzing sketch CS-11M-Step4-Buzzer (saved by Fritzing 0.9.3b)
breadboards: 1

parts:
  Part1 = Arduino Uno (Rev3)
  MIC1 = Microphone

nets:
  N1: Part1.D3_PWM, MIC1.pin2
  N2: Part1.GND, MIC1.pin1
