# Fritzing sketch CS-11M-Step5-ColorLED (saved by Fritzing 0.9.3b)
breadboards: 1

parts:
  Part1 = Arduino Uno (Rev3)
  R1 = Resistor [tolerance=±5% resistance=560 package=THT]
  R2 = Resistor [tolerance=±5% resistance=560 package=THT]
  R3 = Resistor [tolerance=±5% resistance=560 package=THT]
  R4 = Resistor [tolerance=±5% resistance=10k package=THT]
  R5 = Photocell (LDR) [package=THT]
  LED1 = RGB LED - (4 legs) [package="5 mm [THT]"]

nets:
  N1: Part1.A0, R4.Pin_1, R5.pin_0
  N2: Part1.D9_PWM, R3.Pin_1
  N3: Part1.D10_PWM/SS, R2.Pin_1
  N4: Part1.D11_PWM/MOSI, R1.Pin_1
  N5: Part1.5V, R4.Pin_0, LED1.common_anode
  N6: Part1.GND, R5.pin_1
  N7: R1.Pin_0, LED1.red_cathode
  N8: R2.Pin_0, LED1.green_cathode
  N9: R3.Pin_0, LED1.blue_cathode
